# Fritzing sketch nanov3_lm2596s (saved by Fritzing 0.9.3b)

parts:
  Part1 = Arduino Nano (Rev3.0)  # not connected
  M1 = RioRand LM2596
  VCC1 = Battery block 9V
  D1 = Diode [package=diode-1n4148]
  RE1 = KY-040 Rotary encoder [package=THT]  # not connected

nets:
  N1: M1.Pin_1, D1.C
  N2: M1.Pin_2, VCC1.-
  N3: VCC1.+, D1.A

custom parts:
  KY-040 Rotary encoder: KY-040 Rotary Encoder with switch on breakout borad from AZ Delivery
