# Fritzing sketch nanov3_max7219 (saved by Fritzing 0.9.3b)

parts:
  U1 = MAX7219 [package=dil24]
  Part1 = Arduino Nano (Rev3.0)

nets:
  N1: U1.DIN, Part1.A3
  N2: U1.LOAD, Part1.A2
  N3: U1.CLK, Part1.A1
